// Logisim project adder.circ as structural Verilog: 4 circuits, main circuit main
module main (
  input  b2,
  input  a2,
  input  a1,
  input  b1,
  input  a0,
  input  b0,
  output Overflow,
  output s1,
  output s0
);

  wire full_1_soma, full_2_cout, half_adder_1_carry;

  Overflow overflow_1 (.Overflow(Overflow), .a2(a2), .b2(b2), .s2(full_1_soma));
  Full full_1 (.a(a2), .b(b2), .cIn(full_2_cout), .Soma(full_1_soma));  // open: cOut
  Full full_2 (.a(a1), .b(b1), .cIn(half_adder_1_carry), .Soma(s1), .cOut(full_2_cout));
  Half_Adder half_adder_1 (.a(b0), .b(a0), .Soma(s0), .Carry(half_adder_1_carry));
endmodule

module Half_Adder (
  input  a,
  input  b,
  output Soma,
  output Carry
);

  and and_1 (Carry, a, b);
  xor xor_1 (Soma, a, b);

  // Notes on the sheet:
  //   s
endmodule

module Full (
  input  a,
  input  b,
  input  cIn,
  output cOut,
  output Soma
);

  wire half_adder_1_carry, half_adder_1_soma, half_adder_2_carry;

  Half_Adder half_adder_1 (.a(a), .b(b), .Soma(half_adder_1_soma), .Carry(half_adder_1_carry));
  Half_Adder half_adder_2 (.a(half_adder_1_soma), .b(cIn), .Soma(Soma), .Carry(half_adder_2_carry));
  or or_1 (cOut, half_adder_1_carry, half_adder_2_carry);
endmodule

module Overflow (
  input  a2,
  input  b2,
  input  s2,
  output Overflow
);

  wire and_1_out, and_2_out, not_1_out, not_2_out, not_3_out;

  or or_1 (Overflow, and_1_out, and_2_out);
  and and_1 (and_1_out, not_1_out, not_2_out, s2);
  and and_2 (and_2_out, b2, a2, not_3_out);
  not not_1 (not_1_out, a2);
  not not_2 (not_2_out, b2);
  not not_3 (not_3_out, s2);
endmodule
