// Logisim project decoder.circ as structural Verilog: 1 circuit, main circuit main
module main (
  input  x,
  input  y,
  output out_3,
  output out_4,
  output out_5,
  output out_6
);

  wire not_1_out, not_2_out;

  not not_1 (not_1_out, x);
  not not_2 (not_2_out, y);
  and and_1 (out_3, x, y);
  and and_2 (out_4, x, not_2_out);
  and and_3 (out_5, not_1_out, y);
  and and_4 (out_6, not_1_out, not_2_out);
endmodule
