// Logisim project ULA.circ as structural Verilog: 1 circuit, main circuit main
module main (
  input  s2,
  input  s1,
  input  s0,
  input  a0,
  input  a1,
  input  a2,
  input  a3,
  input  a4,
  input  a5,
  input  a6,
  input  a7,
  input  b0,
  input  b1,
  input  b2,
  input  b3,
  input  b4,
  input  b5,
  input  b6,
  input  b7,
  output overflow,
  output r0,
  output r1,
  output r2,
  output r3,
  output r4,
  output r5,
  output r6,
  output r7
);

  wire ADICAO_overflow, DIVISAO_overflow, MULTIPLICACAO_overflow, SUBTRACAO_overflow;
  wire [7:0] ADICAO_r, DIVISAO_quociente, DIVISAO_resto, MULTIPLICACAO_r, SUBTRACAO_r;

  Somador ADICAO (
    .overflow(ADICAO_overflow), .A({a7, a6, a5, a4, a3, a2, a1, a0}), .B({b7, b6, b5, b4, b3, b2, b1, b0}),
    .R(ADICAO_r));
  Subtrador SUBTRACAO (
    .A({a7, a6, a5, a4, a3, a2, a1, a0}), .B({b7, b6, b5, b4, b3, b2, b1, b0}),
    .overflow(SUBTRACAO_overflow), .R(SUBTRACAO_r));
  Multiplicador MULTIPLICACAO (
    .A({a7, a6, a5, a4, a3, a2, a1, a0}), .B({b7, b6, b5, b4, b3, b2, b1, b0}), .R(MULTIPLICACAO_r),
    .overflow(MULTIPLICACAO_overflow));
  Divisor DIVISAO (
    .A({a7, a6, a5, a4, a3, a2, a1, a0}), .B({b7, b6, b5, b4, b3, b2, b1, b0}), .RESTO(DIVISAO_resto),
    .QUOCIENTE(DIVISAO_quociente), .overflow(DIVISAO_overflow));
  Multiplexer #(.select(3)) multiplexer_1 (
    .in0(ADICAO_overflow), .in1(SUBTRACAO_overflow), .in2(MULTIPLICACAO_overflow), .in3(DIVISAO_overflow),
    .in4(DIVISAO_overflow), .out(overflow), .sel({s2, s1, s0}));  // open: in5, in6, in7, en
  Multiplexer #(.select(3), .width(8)) multiplexer_2 (
    .in0(ADICAO_r), .in1(SUBTRACAO_r), .in2(MULTIPLICACAO_r), .in3(DIVISAO_quociente), .in4(DIVISAO_resto),
    .out({r7, r6, r5, r4, r3, r2, r1, r0}), .sel({s2, s1, s0}));  // open: in5, in6, in7, en
endmodule
