// Logisim project adicao.circ as structural Verilog: 4 circuits, main circuit Somador
module Somador (
  input  [7:0] A,
  input  [7:0] B,
  output [7:0] R,
  output overflow
);

  wire FA_2_carry_out, FA_3_carry_out, FA_4_carry_out, FA_5_carry_out, FA_6_carry_out, FA_7_carry_out,
       HA_carry_out;

  Overflow u_Overflow (.a7(A[7]), .b7(B[7]), .r7(R[7]), .Overflow(overflow));
  Full_Adder FA (.a(A[7]), .b(B[7]), .Soma(R[7]), .Carry_In(FA_2_carry_out));  // open: Carry_Out
  Full_Adder FA_2 (.a(A[6]), .b(B[6]), .Soma(R[6]), .Carry_In(FA_3_carry_out), .Carry_Out(FA_2_carry_out));
  Full_Adder FA_3 (.a(A[5]), .b(B[5]), .Soma(R[5]), .Carry_In(FA_4_carry_out), .Carry_Out(FA_3_carry_out));
  Full_Adder FA_4 (.a(A[4]), .b(B[4]), .Soma(R[4]), .Carry_In(FA_5_carry_out), .Carry_Out(FA_4_carry_out));
  Full_Adder FA_5 (.a(A[3]), .b(B[3]), .Soma(R[3]), .Carry_In(FA_6_carry_out), .Carry_Out(FA_5_carry_out));
  Full_Adder FA_6 (.a(A[2]), .b(B[2]), .Soma(R[2]), .Carry_In(FA_7_carry_out), .Carry_Out(FA_6_carry_out));
  Full_Adder FA_7 (.a(A[1]), .b(B[1]), .Soma(R[1]), .Carry_In(HA_carry_out), .Carry_Out(FA_7_carry_out));
  Half_Adder HA (.a(A[0]), .b(B[0]), .Soma(R[0]), .Carry_Out(HA_carry_out));
endmodule

module Full_Adder (
  input  Carry_In,
  input  a,
  input  b,
  output Soma,
  output Carry_Out
);

  wire HA_2_carry_out, HA_carry_out, HA_soma;

  Half_Adder HA (.a(a), .b(b), .Soma(HA_soma), .Carry_Out(HA_carry_out));
  or or_1 (Carry_Out, HA_carry_out, HA_2_carry_out);
  Half_Adder HA_2 (.a(Carry_In), .b(HA_soma), .Soma(Soma), .Carry_Out(HA_2_carry_out));
endmodule

module Half_Adder (
  input  a,
  input  b,
  output Soma,
  output Carry_Out
);

  and and_1 (Carry_Out, a, b);
  xor xor_1 (Soma, a, b);
endmodule

module Overflow (
  input  a7,
  input  b7,
  input  r7,
  output Overflow
);

  wire and_1_out, and_2_out, not_1_out, not_2_out, not_3_out;

  not not_1 (not_1_out, a7);
  not not_2 (not_2_out, b7);
  not not_3 (not_3_out, r7);
  and and_1 (and_1_out, not_1_out, not_2_out, r7);
  and and_2 (and_2_out, a7, b7, not_3_out);
  or or_1 (Overflow, and_1_out, and_2_out);
endmodule
