// Logisim project divisao.circ as structural Verilog: 4 circuits, main circuit Divisor
module Divisor (
  input  [7:0] A,
  input  [7:0] B,
  output [7:0] RESTO,
  output [7:0] QUOCIENTE,
  output overflow
);

  wire not_1_out, xor_1_out;
  wire [0:0] Valor_Abs_out_3, Valor_Abs_out_4, Valor_Abs_out_5;
  wire [6:4] Valor_Abs_out;
  wire [7:0] div_mod_1_r, div_mod_2_r, div_mod_4_r, div_mod_5_r, div_mod_6_r, div_mod_7_q, Negativo_out,
       Valor_Abs_2_out, Valor_Abs_out_2;
  wire [7:7] and_1_out, div_mod_3_r;

  Valor_Abs Valor_Abs (
    .IN(A),
    .OUT({div_mod_7_q[7], Valor_Abs_out, Valor_Abs_out_2[0], Valor_Abs_out_3[0], Valor_Abs_out_4[0], Valor_Abs_out_5[0]}));
  Valor_Abs Valor_Abs_2 (.IN(B), .OUT(Valor_Abs_2_out));
  not not_1 (not_1_out, Valor_Abs_out[6]);
  and and_1 (and_1_out[7], Valor_Abs_out[6], not_1_out);
  Div_Mod div_mod_1 (
    .A({{7{and_1_out[7]}}, Valor_Abs_out[6]}), .B(Valor_Abs_2_out), .q(div_mod_7_q[6]), .R(div_mod_1_r));
  Div_Mod div_mod_2 (
    .A({div_mod_1_r[6:0], Valor_Abs_out[5]}), .B(Valor_Abs_2_out), .q(div_mod_7_q[5]), .R(div_mod_2_r));
  Div_Mod div_mod_3 (
    .A({div_mod_2_r[6:0], Valor_Abs_out[4]}), .B(Valor_Abs_2_out), .q(div_mod_7_q[4]),
    .R({div_mod_3_r[7], Valor_Abs_out_2[7:1]}));
  Div_Mod div_mod_4 (.A(Valor_Abs_out_2), .B(Valor_Abs_2_out), .q(div_mod_7_q[3]), .R(div_mod_4_r));
  Div_Mod div_mod_5 (
    .A({div_mod_4_r[6:0], Valor_Abs_out_3[0]}), .B(Valor_Abs_2_out), .q(div_mod_7_q[2]), .R(div_mod_5_r));
  Div_Mod div_mod_6 (
    .A({div_mod_5_r[6:0], Valor_Abs_out_4[0]}), .B(Valor_Abs_2_out), .q(div_mod_7_q[1]), .R(div_mod_6_r));
  Div_Mod div_mod_7 (.A({div_mod_6_r[6:0], Valor_Abs_out_5[0]}), .B(Valor_Abs_2_out), .q(div_mod_7_q[0]), .R(RESTO));
  Inverte_e_Soma_1 Negativo (.IN(div_mod_7_q), .OUT(Negativo_out));
  Multiplexer #(.width(8)) multiplexer_1 (
    .in0(div_mod_7_q), .in1(Negativo_out), .out(QUOCIENTE), .sel(xor_1_out));  // open: en
  nor nor_1 (overflow, Valor_Abs_2_out[0], Valor_Abs_2_out[1], Valor_Abs_2_out[2], Valor_Abs_2_out[3], Valor_Abs_2_out[4], Valor_Abs_2_out[5], Valor_Abs_2_out[6], Valor_Abs_2_out[7]);
  xor xor_1 (xor_1_out, A[7], B[7]);
endmodule

module Div_Mod (
  input  [7:0] A,
  input  [7:0] B,
  output q,
  output [7:0] R
);

  wire [7:0] SUBTRADOR_r;

  Subtrador SUBTRADOR (.A(A), .B(B), .R(SUBTRADOR_r));  // open: overflow
  not not_1 (q, SUBTRADOR_r[7]);
  Multiplexer #(.width(8)) multiplexer_1 (.in0(A), .in1(SUBTRADOR_r), .out(R), .sel(q));  // open: en
endmodule

module Valor_Abs (
  input  [7:0] IN,
  output [7:0] OUT
);

  wire [7:0] Inverte_e_Soma_1_out;

  Inverte_e_Soma_1 Inverte_e_Soma_1 (.IN(IN), .OUT(Inverte_e_Soma_1_out));
  Multiplexer #(.width(8)) multiplexer_1 (.in0(IN), .in1(Inverte_e_Soma_1_out), .out(OUT), .sel(IN[7]));  // open: en
endmodule

module Inverte_e_Soma_1 (
  input  [7:0] IN,
  output [7:0] OUT
);

  wire [7:0] not_1_out;

  not not_1 (not_1_out[0], IN[0]);
  not not_2 (not_1_out[1], IN[1]);
  not not_3 (not_1_out[2], IN[2]);
  not not_4 (not_1_out[3], IN[3]);
  not not_5 (not_1_out[4], IN[4]);
  not not_6 (not_1_out[5], IN[5]);
  not not_7 (not_1_out[6], IN[6]);
  not not_8 (not_1_out[7], IN[7]);
  Somador SOMADOR (.A(not_1_out), .B(8'h1), .R(OUT));  // open: overflow
endmodule
