// Logisim project multiplicacao.circ as structural Verilog: 4 circuits, main circuit Multiplicador
module Half_Adder (
  input  a,
  input  b,
  output Soma,
  output Carry_Out
);

  and and_1 (Carry_Out, a, b);
  xor xor_1 (Soma, a, b);
endmodule

module Full_Adder (
  input  Carry_In,
  input  a,
  input  b,
  output Soma,
  output Carry_Out
);

  wire half_adder_1_carry_out, half_adder_1_soma, half_adder_2_carry_out;

  Half_Adder half_adder_1 (.a(a), .b(b), .Soma(half_adder_1_soma), .Carry_Out(half_adder_1_carry_out));
  or or_1 (Carry_Out, half_adder_1_carry_out, half_adder_2_carry_out);
  Half_Adder half_adder_2 (.a(Carry_In), .b(half_adder_1_soma), .Soma(Soma), .Carry_Out(half_adder_2_carry_out));
endmodule

module AND_8_bits_com_1_bit (
  input  a,
  input  [7:0] B,
  output r0,
  output r1,
  output r2,
  output r3,
  output r4,
  output r5,
  output r6,
  output r7
);

  and and_1 (r0, B[0], a);
  and and_2 (r1, B[1], a);
  and and_3 (r2, B[2], a);
  and and_4 (r3, B[3], a);
  and and_5 (r4, B[4], a);
  and and_6 (r5, B[5], a);
  and and_7 (r6, B[6], a);
  and and_8 (r7, B[7], a);
endmodule

module Multiplicador (
  input  [7:0] A,
  input  [7:0] B,
  output [7:0] R,
  output overflow
);

  wire and_2_r0, and_2_r1, and_2_r2, and_2_r3, and_2_r4, and_2_r5, and_2_r6, and_2_r7, and_3_r0, and_3_r1,
       and_3_r2, and_3_r3, and_3_r4, and_3_r5, and_3_r6, and_3_r7, and_4_r0, and_4_r1, and_4_r2, and_4_r3,
       and_4_r4, and_4_r5, and_4_r6, and_4_r7, and_5_r0, and_5_r1, and_5_r2, and_5_r3, and_5_r4, and_5_r5,
       and_5_r6, and_5_r7, and_6_r0, and_6_r1, and_6_r2, and_6_r3, and_6_r4, and_6_r5, and_6_r6, and_6_r7,
       and_7_r0, and_7_r1, and_7_r2, and_7_r3, and_7_r4, and_7_r5, and_7_r6, and_7_r7, and_8_r0, and_8_r1,
       and_8_r2, and_8_r3, and_8_r4, and_8_r5, and_8_r6, and_8_r7, and_r1, and_r2, and_r3, and_r4, and_r5,
       and_r6, and_r7, full_adder_1_carry_out, full_adder_1_soma, full_adder_2_carry_out, full_adder_2_soma,
       full_adder_3_carry_out, full_adder_3_soma, full_adder_4_carry_out, full_adder_4_soma,
       full_adder_5_carry_out, full_adder_5_soma, full_adder_6_carry_out, full_adder_6_soma,
       full_adder_7_carry_out, full_adder_7_soma, full_adder_8_carry_out, full_adder_8_soma,
       full_adder_9_carry_out, full_adder_9_soma, full_adder_10_carry_out, full_adder_10_soma,
       full_adder_11_carry_out, full_adder_11_soma, full_adder_12_carry_out, full_adder_12_soma,
       full_adder_13_carry_out, full_adder_13_soma, full_adder_14_carry_out, full_adder_14_soma,
       full_adder_15_carry_out, full_adder_15_soma, full_adder_16_carry_out, full_adder_16_soma,
       full_adder_17_carry_out, full_adder_17_soma, full_adder_18_carry_out, full_adder_18_soma,
       full_adder_19_carry_out, full_adder_19_soma, full_adder_20_carry_out, full_adder_20_soma,
       full_adder_21_carry_out, full_adder_21_soma, half_adder_1_carry_out, half_adder_2_carry_out,
       half_adder_3_carry_out, half_adder_4_carry_out, half_adder_5_carry_out, half_adder_6_carry_out,
       half_adder_7_carry_out, or_1_out, or_2_out, or_3_out, or_4_out, or_5_out, or_6_out, or_7_out,
       xor_1_out;
  wire [7:0] and_r0, Negativo_out, Valor_Abs_2_out, Valor_Abs_out;

  Valor_Abs Valor_Abs (.IN(A), .OUT(Valor_Abs_out));
  Valor_Abs Valor_Abs_2 (.IN(B), .OUT(Valor_Abs_2_out));
  AND_8_bits_com_1_bit \and  (
    .a(Valor_Abs_out[0]), .B(Valor_Abs_2_out), .r0(and_r0[0]), .r1(and_r1), .r2(and_r2), .r3(and_r3),
    .r4(and_r4), .r5(and_r5), .r6(and_r6), .r7(and_r7));
  AND_8_bits_com_1_bit and_2 (
    .a(Valor_Abs_out[1]), .B(Valor_Abs_2_out), .r0(and_2_r0), .r1(and_2_r1), .r2(and_2_r2), .r3(and_2_r3),
    .r4(and_2_r4), .r5(and_2_r5), .r6(and_2_r6), .r7(and_2_r7));
  AND_8_bits_com_1_bit and_3 (
    .a(Valor_Abs_out[2]), .B(Valor_Abs_2_out), .r0(and_3_r0), .r1(and_3_r1), .r2(and_3_r2), .r3(and_3_r3),
    .r4(and_3_r4), .r5(and_3_r5), .r6(and_3_r6), .r7(and_3_r7));
  AND_8_bits_com_1_bit and_4 (
    .a(Valor_Abs_out[3]), .B(Valor_Abs_2_out), .r0(and_4_r0), .r1(and_4_r1), .r2(and_4_r2), .r3(and_4_r3),
    .r4(and_4_r4), .r5(and_4_r5), .r6(and_4_r6), .r7(and_4_r7));
  AND_8_bits_com_1_bit and_5 (
    .a(Valor_Abs_out[4]), .B(Valor_Abs_2_out), .r0(and_5_r0), .r1(and_5_r1), .r2(and_5_r2), .r3(and_5_r3),
    .r4(and_5_r4), .r5(and_5_r5), .r6(and_5_r6), .r7(and_5_r7));
  AND_8_bits_com_1_bit and_6 (
    .a(Valor_Abs_out[5]), .B(Valor_Abs_2_out), .r0(and_6_r0), .r1(and_6_r1), .r2(and_6_r2), .r3(and_6_r3),
    .r4(and_6_r4), .r5(and_6_r5), .r6(and_6_r6), .r7(and_6_r7));
  AND_8_bits_com_1_bit and_7 (
    .a(Valor_Abs_out[6]), .B(Valor_Abs_2_out), .r0(and_7_r0), .r1(and_7_r1), .r2(and_7_r2), .r3(and_7_r3),
    .r4(and_7_r4), .r5(and_7_r5), .r6(and_7_r6), .r7(and_7_r7));
  AND_8_bits_com_1_bit and_8 (
    .a(Valor_Abs_out[7]), .B(Valor_Abs_2_out), .r0(and_8_r0), .r1(and_8_r1), .r2(and_8_r2), .r3(and_8_r3),
    .r4(and_8_r4), .r5(and_8_r5), .r6(and_8_r6), .r7(and_8_r7));
  or or_1 (or_1_out, and_6_r7, and_6_r6, and_6_r5, and_6_r4, and_6_r3, or_5_out);
  or or_2 (or_2_out, and_8_r1, and_8_r2, and_8_r3, and_8_r4, and_8_r5, and_8_r6, and_8_r7);
  or or_3 (or_3_out, and_3_r7, and_3_r6, and_2_r7);
  or or_4 (or_4_out, and_4_r7, and_4_r6, and_4_r5, or_3_out);
  or or_5 (or_5_out, and_5_r7, and_5_r6, and_5_r5, and_5_r4, or_4_out);
  or or_6 (or_6_out, or_1_out, and_7_r7, and_7_r6, and_7_r5, and_7_r4, and_7_r3, and_7_r2);
  Half_Adder half_adder_1 (.a(and_r1), .b(and_2_r0), .Soma(and_r0[1]), .Carry_Out(half_adder_1_carry_out));
  Full_Adder full_adder_1 (
    .a(and_r2), .b(and_2_r1), .Soma(full_adder_1_soma), .Carry_In(half_adder_1_carry_out),
    .Carry_Out(full_adder_1_carry_out));
  Full_Adder full_adder_2 (
    .a(and_r3), .b(and_2_r2), .Soma(full_adder_2_soma), .Carry_In(full_adder_1_carry_out),
    .Carry_Out(full_adder_2_carry_out));
  Full_Adder full_adder_3 (
    .a(and_r4), .b(and_2_r3), .Soma(full_adder_3_soma), .Carry_In(full_adder_2_carry_out),
    .Carry_Out(full_adder_3_carry_out));
  Full_Adder full_adder_4 (
    .a(and_r5), .b(and_2_r4), .Soma(full_adder_4_soma), .Carry_In(full_adder_3_carry_out),
    .Carry_Out(full_adder_4_carry_out));
  Full_Adder full_adder_5 (
    .a(and_r6), .b(and_2_r5), .Soma(full_adder_5_soma), .Carry_In(full_adder_4_carry_out),
    .Carry_Out(full_adder_5_carry_out));
  Full_Adder full_adder_6 (
    .a(and_r7), .b(and_2_r6), .Soma(full_adder_6_soma), .Carry_In(full_adder_5_carry_out),
    .Carry_Out(full_adder_6_carry_out));
  Half_Adder half_adder_2 (.a(full_adder_1_soma), .b(and_3_r0), .Soma(and_r0[2]), .Carry_Out(half_adder_2_carry_out));
  Full_Adder full_adder_7 (
    .a(full_adder_2_soma), .b(and_3_r1), .Soma(full_adder_7_soma), .Carry_In(half_adder_2_carry_out),
    .Carry_Out(full_adder_7_carry_out));
  Full_Adder full_adder_8 (
    .a(full_adder_3_soma), .b(and_3_r2), .Soma(full_adder_8_soma), .Carry_In(full_adder_7_carry_out),
    .Carry_Out(full_adder_8_carry_out));
  Full_Adder full_adder_9 (
    .a(full_adder_4_soma), .b(and_3_r3), .Soma(full_adder_9_soma), .Carry_In(full_adder_8_carry_out),
    .Carry_Out(full_adder_9_carry_out));
  Full_Adder full_adder_10 (
    .a(full_adder_5_soma), .b(and_3_r4), .Soma(full_adder_10_soma), .Carry_In(full_adder_9_carry_out),
    .Carry_Out(full_adder_10_carry_out));
  Full_Adder full_adder_11 (
    .a(full_adder_6_soma), .b(and_3_r5), .Soma(full_adder_11_soma), .Carry_In(full_adder_10_carry_out),
    .Carry_Out(full_adder_11_carry_out));
  Half_Adder half_adder_3 (.a(full_adder_7_soma), .b(and_4_r0), .Soma(and_r0[3]), .Carry_Out(half_adder_3_carry_out));
  Full_Adder full_adder_12 (
    .a(full_adder_8_soma), .b(and_4_r1), .Soma(full_adder_12_soma), .Carry_In(half_adder_3_carry_out),
    .Carry_Out(full_adder_12_carry_out));
  Full_Adder full_adder_13 (
    .a(full_adder_9_soma), .b(and_4_r2), .Soma(full_adder_13_soma), .Carry_In(full_adder_12_carry_out),
    .Carry_Out(full_adder_13_carry_out));
  Full_Adder full_adder_14 (
    .a(full_adder_10_soma), .b(and_4_r3), .Soma(full_adder_14_soma), .Carry_In(full_adder_13_carry_out),
    .Carry_Out(full_adder_14_carry_out));
  Full_Adder full_adder_15 (
    .a(full_adder_11_soma), .b(and_4_r4), .Soma(full_adder_15_soma), .Carry_In(full_adder_14_carry_out),
    .Carry_Out(full_adder_15_carry_out));
  xor xor_1 (xor_1_out, A[7], B[7]);
  Half_Adder half_adder_4 (.a(full_adder_12_soma), .b(and_5_r0), .Soma(and_r0[4]), .Carry_Out(half_adder_4_carry_out));
  Full_Adder full_adder_16 (
    .a(full_adder_13_soma), .b(and_5_r1), .Soma(full_adder_16_soma), .Carry_In(half_adder_4_carry_out),
    .Carry_Out(full_adder_16_carry_out));
  Full_Adder full_adder_17 (
    .a(full_adder_14_soma), .b(and_5_r2), .Soma(full_adder_17_soma), .Carry_In(full_adder_16_carry_out),
    .Carry_Out(full_adder_17_carry_out));
  Full_Adder full_adder_18 (
    .a(full_adder_15_soma), .b(and_5_r3), .Soma(full_adder_18_soma), .Carry_In(full_adder_17_carry_out),
    .Carry_Out(full_adder_18_carry_out));
  Half_Adder half_adder_5 (.a(full_adder_16_soma), .b(and_6_r0), .Soma(and_r0[5]), .Carry_Out(half_adder_5_carry_out));
  Full_Adder full_adder_19 (
    .a(full_adder_17_soma), .b(and_6_r1), .Soma(full_adder_19_soma), .Carry_In(half_adder_5_carry_out),
    .Carry_Out(full_adder_19_carry_out));
  Full_Adder full_adder_20 (
    .a(full_adder_18_soma), .b(and_6_r2), .Soma(full_adder_20_soma), .Carry_In(full_adder_19_carry_out),
    .Carry_Out(full_adder_20_carry_out));
  Half_Adder half_adder_6 (.a(full_adder_19_soma), .b(and_7_r0), .Soma(and_r0[6]), .Carry_Out(half_adder_6_carry_out));
  Full_Adder full_adder_21 (
    .a(full_adder_20_soma), .b(and_7_r1), .Soma(full_adder_21_soma), .Carry_In(half_adder_6_carry_out),
    .Carry_Out(full_adder_21_carry_out));
  Half_Adder half_adder_7 (.a(full_adder_21_soma), .b(and_8_r0), .Soma(and_r0[7]), .Carry_Out(half_adder_7_carry_out));
  or or_7 (or_7_out, or_6_out, or_2_out, half_adder_7_carry_out, full_adder_21_carry_out, full_adder_20_carry_out, full_adder_18_carry_out, full_adder_15_carry_out, full_adder_11_carry_out, full_adder_6_carry_out);
  Inverte_e_Soma_1 Negativo (.IN(and_r0), .OUT(Negativo_out));
  Multiplexer #(.width(8)) multiplexer_1 (.in0(and_r0), .in1(Negativo_out), .out(R), .sel(xor_1_out));  // open: en
  or or_8 (overflow, and_r0[7], or_7_out);
endmodule
