// Logisim project subtracao.circ as structural Verilog: 4 circuits, main circuit Subtrador
module Subtrador (
  input  [7:0] A,
  input  [7:0] B,
  output overflow,
  output [7:0] R
);

  wire FA_2_c_out, FA_3_c_out, FA_4_c_out, FA_5_c_out, FA_6_c_out, FA_7_c_out, FA_c_out, xor_1_out,
       xor_2_out, xor_3_out, xor_4_out, xor_5_out, xor_6_out, xor_7_out, xor_8_out;

  xor xor_1 (xor_1_out, 1'b1, B[0]);
  FA FA (.c_in(1'b1), .A(A[0]), .B(xor_1_out), .Resultado(R[0]), .c_out(FA_c_out));
  xor xor_2 (xor_2_out, 1'b1, B[1]);
  FA FA_2 (.c_in(FA_c_out), .A(A[1]), .B(xor_2_out), .Resultado(R[1]), .c_out(FA_2_c_out));
  xor xor_3 (xor_3_out, 1'b1, B[2]);
  FA FA_3 (.c_in(FA_2_c_out), .A(A[2]), .B(xor_3_out), .Resultado(R[2]), .c_out(FA_3_c_out));
  xor xor_4 (xor_4_out, 1'b1, B[3]);
  FA FA_4 (.c_in(FA_3_c_out), .A(A[3]), .B(xor_4_out), .Resultado(R[3]), .c_out(FA_4_c_out));
  xor xor_5 (xor_5_out, 1'b1, B[4]);
  FA FA_5 (.c_in(FA_4_c_out), .A(A[4]), .B(xor_5_out), .Resultado(R[4]), .c_out(FA_5_c_out));
  FA FA_6 (.c_in(FA_5_c_out), .A(A[5]), .B(xor_6_out), .Resultado(R[5]), .c_out(FA_6_c_out));
  xor xor_6 (xor_6_out, 1'b1, B[5]);
  FA FA_7 (.c_in(FA_6_c_out), .A(A[6]), .B(xor_7_out), .Resultado(R[6]), .c_out(FA_7_c_out));
  xor xor_7 (xor_7_out, 1'b1, B[6]);
  FA FA_8 (.c_in(FA_7_c_out), .A(A[7]), .B(xor_8_out), .Resultado(R[7]));  // open: c_out
  xor xor_8 (xor_8_out, 1'b1, B[7]);
  Overflow u_overflow (.a7(A[7]), .b7(xor_8_out), .r7(R[7]), .Overflow(overflow));
endmodule

module HA (
  input  A,
  input  B,
  output Resultado,
  output out_4
);

  and and_1 (out_4, A, B);
  xor xor_1 (Resultado, A, B);
endmodule

module FA (
  input  c_in,
  input  A,
  input  B,
  output Resultado,
  output c_out
);

  wire HA_2_out_4, HA_out_4, HA_resultado;

  HA HA (.A(A), .B(B), .out_4(HA_out_4), .Resultado(HA_resultado));
  or or_1 (c_out, HA_out_4, HA_2_out_4);
  HA HA_2 (.A(c_in), .B(HA_resultado), .out_4(HA_2_out_4), .Resultado(Resultado));
endmodule

module Overflow (
  input  a7,
  input  b7,
  input  r7,
  output Overflow
);

  wire and_1_out, and_2_out, not_1_out, not_2_out, not_3_out;

  not not_1 (not_1_out, a7);
  not not_2 (not_2_out, b7);
  not not_3 (not_3_out, r7);
  and and_1 (and_1_out, not_1_out, not_2_out, r7);
  and and_2 (and_2_out, a7, b7, not_3_out);
  or or_1 (Overflow, and_1_out, and_2_out);
endmodule
